# Fritzing sketch ultrasonic_distance_sensing (saved by Fritzing 0.9.3b)
breadboards: 1

parts:
  R1 = BBC MicroBit
  hc-sr1 = hc-sr04
  J1 = Basic Servo
  VCC1 = Battery block 9V

nets:
  GND: R1.GND, hc-sr1.GND, J1.gnd, VCC1.-
  N1: R1.P4_ANALOG_IN, hc-sr1.Trig
  N2: R1.P0_ANALOG_IN, J1.pulse
  N3: J1.vcc, VCC1.+

custom parts:
  BBC MicroBit: The BBC MICRO:BIT
